# Fritzing sketch GasSensorGrenadeBoard V2.0 (saved by Fritzing 0.9.1b)
circuit board: 1.9696cm x 5.49451cm
breadboards: 1

parts:
  NANO = Arduino Nano (Rev3.0)
  VCC = Battery
  TX = mystery part, 3 pins [chip_label=?]
  MQ2 = female pin header, 4 pins [form="♀ (female)"]

nets:
  N1: NANO.GND, VCC.-, TX.pin1, MQ2.pin4
  N2: NANO.D3, TX.pin3
  N3: NANO.VIN, VCC.+
  N4: NANO.5V, TX.pin2, MQ2.pin1
  N5: NANO.A0, MQ2.pin3

notes:
  www.mkme.org
  Version 2.0
  Gas Sensor Grenade
